// Logisim project MIPS.circ as structural Verilog: 1 circuit, main circuit main
module main (
);

  wire alu_1_zero, and_1_out, button_1_out, CLK, controlunit_1_out_4, controlunit_1_out_5,
       controlunit_1_out_6, controlunit_1_out_7, controlunit_1_out_8, controlunit_1_out_9,
       controlunit_1_out_10;
  wire [3:0] adder_1_out_2, controlunit_1_out_11;
  wire [4:0] multiplexer_3_out;
  wire [27:0] adder_1_out, bit_extender_1_out, shifter_1_out;
  wire [31:0] adder_2_out, alu_1_alu_result, bit_extender_2_out, datamem_1_rd, instmem_1_out_2,
       multiplexer_1_out, multiplexer_2_out, multiplexer_4_out, multiplexer_5_out, PC_q, regfile32_1_rd1,
       regfile32_1_rd2, shifter_2_out;

  Clock clock_1 (.out(CLK));
  Multiplexer #(.width(32)) multiplexer_1 (
    .in0({adder_1_out_2, adder_1_out}), .in1(adder_2_out), .out(multiplexer_1_out), .sel(and_1_out));  // open: en
  Register #(.width(32)) PC (.D(multiplexer_2_out), .Q(PC_q), .clk(CLK), .clr(button_1_out));  // open: en
  Multiplexer #(.width(32)) multiplexer_2 (
    .in0(multiplexer_1_out), .in1({adder_1_out_2, shifter_1_out}), .out(multiplexer_2_out),
    .sel(controlunit_1_out_4));  // open: en
  Button button_1 (.out(button_1_out));
  Adder #(.width(32)) adder_1 (.a(PC_q), .b(32'h4), .out({adder_1_out_2, adder_1_out}));  // open: cin, cout
  InstMem instmem_1 (.A(PC_q), .out_2(instmem_1_out_2));
  assign bit_extender_1_out = {{2{instmem_1_out_2[25]}}, instmem_1_out_2[25:0]};  // Bit_Extender bit_extender_1
  ControlUnit controlunit_1 (
    .out_4(controlunit_1_out_4), .in_1(instmem_1_out_2[31:26]), .in_2(instmem_1_out_2[5:0]),
    .out_5(controlunit_1_out_5), .out_6(controlunit_1_out_6), .out_7(controlunit_1_out_7),
    .out_8(controlunit_1_out_8), .out_9(controlunit_1_out_9), .out_10(controlunit_1_out_10),
    .out_11(controlunit_1_out_11));  // open: out_3
  Shifter #(.width(28)) shifter_1 (.in(bit_extender_1_out), .\dist (5'b00010), .out(shifter_1_out));
  RegFile32 regfile32_1 (
    .AD1(instmem_1_out_2[25:21]), .AD2(instmem_1_out_2[20:16]), .CLK(CLK), .WE(controlunit_1_out_10),
    .AD3(multiplexer_3_out), .WD3(multiplexer_5_out), .RD1(regfile32_1_rd1), .RD2(regfile32_1_rd2));
  Multiplexer #(.width(5)) multiplexer_3 (
    .in0(instmem_1_out_2[20:16]), .in1(instmem_1_out_2[15:11]), .out(multiplexer_3_out),
    .sel(controlunit_1_out_9));  // open: en
  Multiplexer #(.width(32)) multiplexer_4 (
    .in0(regfile32_1_rd2), .in1(bit_extender_2_out), .out(multiplexer_4_out), .sel(controlunit_1_out_8));  // open: en
  assign bit_extender_2_out = {{16{instmem_1_out_2[15]}}, instmem_1_out_2[15:0]};  // Bit_Extender bit_extender_2
  Shifter #(.width(32)) shifter_2 (.in(bit_extender_2_out), .\dist (5'b00010), .out(shifter_2_out));
  ALU alu_1 (
    .SrcA(regfile32_1_rd1), .SrcB(multiplexer_4_out), .ALU_Control(controlunit_1_out_11), .Zero(alu_1_zero),
    .ALU_Result(alu_1_alu_result));
  Adder #(.width(32)) adder_2 (
    .a(shifter_2_out), .b({adder_1_out_2, adder_1_out}), .out(adder_2_out));  // open: cin, cout
  and and_1 (and_1_out, controlunit_1_out_7, alu_1_zero);
  DataMem datamem_1 (
    .CLK(CLK), .WE(controlunit_1_out_6), .WD(regfile32_1_rd2), .A(alu_1_alu_result), .RD(datamem_1_rd));
  Multiplexer #(.width(32)) multiplexer_5 (
    .in0(alu_1_alu_result), .in1(datamem_1_rd), .out(multiplexer_5_out), .sel(controlunit_1_out_5));  // open: en
endmodule
